// Logisim project ben_eater_602_logism.circ as structural Verilog: 1 circuit, main circuit main
module main (
  output w0r1,
  output [15:0] ADDR
);

  wire nand_1_out, nand_2_out, reset_out, w65c02s_pdip_40_1_p18, w65c02s_pdip_40_1_p20, w65c22_1_p1;
  wire [2:0] undriven;
  wire [7:0] rom_1_data, w65c22_1_p8, w65c22_1_p10;

  ROM #(.addrWidth(16)) rom_1 (.addr(ADDR), .data(rom_1_data));
  // W65C02S__PDIP_40 w65c02s_pdip_40_1: pin names not known; wires that end beside it: ADDR, 1'b1, 1'b1, 1'b1, 1'b1, ADDR[0], ADDR[1], ADDR[2], ADDR[3], ADDR[4], ADDR[5], ADDR[6], ADDR[7], ADDR[8], ADDR[9], ADDR[10], ADDR[11], w65c02s_pdip_40_1_p18, 1'b1, w65c02s_pdip_40_1_p20, 1'b1, w0r1, rom_1_data[0], rom_1_data[1], rom_1_data[2], rom_1_data[3], rom_1_data[4], rom_1_data[5], rom_1_data[6], rom_1_data[7], ADDR[12], ADDR[13], ADDR[14], ADDR[15], 1'b0
  Clock #(.highDuration(2), .lowDuration(2)) clock_1 (.out(w65c02s_pdip_40_1_p20));
  Pull_Resistor #(.pull(1)) pull_resistor_1 (.node(w65c02s_pdip_40_1_p18));
  Button reset (.out(reset_out));
  not not_1 (w65c02s_pdip_40_1_p18, reset_out);
  // Probe on rom_1_data
  nand nand_1 (nand_1_out, undriven[0], undriven[0]);
  nand nand_2 (nand_2_out, nand_1_out, undriven[1]);
  // W65C22 w65c22_1: pin names not known; wires that end beside it: w65c22_1_p1, w65c02s_pdip_40_1_p20, w65c02s_pdip_40_1_p18, undriven[2], nand_2_out, w0r1, w65c22_1_p1, w65c22_1_p8, w65c22_1_p1, w65c22_1_p10
  LedBar ledbar_1 (
    .led0(w65c22_1_p8[7]), .led1(w65c22_1_p8[6]), .led2(w65c22_1_p8[5]), .led3(w65c22_1_p8[4]),
    .led4(w65c22_1_p8[3]), .led5(w65c22_1_p8[2]), .led6(w65c22_1_p8[1]), .led7(w65c22_1_p8[0]));
  LedBar ledbar_2 (
    .led0(w65c22_1_p10[7]), .led1(w65c22_1_p10[6]), .led2(w65c22_1_p10[5]), .led3(w65c22_1_p10[4]),
    .led4(w65c22_1_p10[3]), .led5(w65c22_1_p10[2]), .led6(w65c22_1_p10[1]), .led7(w65c22_1_p10[0]));

  // Notes on the sheet:
  //   contents of rom_1 (hex, n*v repeats v):
  //   a9 42 8d 0 60 65527*ea 0 0 ea ea
endmodule
